// Logisim project Demo CPU Restored.circ as structural Verilog: 17 circuits, main circuit CPUCore
module CPUCore (
);

  wire button_1_out, button_2_out, clearram_1_clockout, clearram_1_resetout, controlunit_1_acc_set,
       controlunit_1_decsp, controlunit_1_flags_set, controlunit_1_gpr_enable, controlunit_1_gpr_set,
       controlunit_1_gpr_store, controlunit_1_incsp, controlunit_1_ir_set, controlunit_1_out_enable,
       controlunit_1_out_set, controlunit_1_pc_load, controlunit_1_pc_set, controlunit_1_ram_enable,
       controlunit_1_ram_set, controlunit_1_ram_store, controlunit_1_sp_out, controlunit_1_temp_highset,
       controlunit_1_temp_lowset, controlunit_1_tempselect, dipswitch_1_sw1, dipswitch_1_sw2, or_1_out,
       or_2_out, ramgate_1_clockout, ramgate_1_loadout, ramgate_1_storeout;
  wire [1:0] arithmaticlogicunit_1_flagsout, flags_1_flagsoutalu, flags_1_flagsoutcu;
  wire [2:0] controlunit_1_regselect;
  wire [3:0] controlunit_1_aluoperation;
  wire [7:0] accumulator_1_dataout, arithmaticlogicunit_1_output, clearram_1_dataout,
       gpr_block_1_stack_pointer_out, instructionreg_1_instructionout;
  wire [15:0] clearram_1_addrout, multiplexer_1_out, multiplexer_2_out, programcounter_1_addressout,
       ramgate_1_addrout, tempaddress_1_addressout;

  Button button_1 (.out(button_1_out));
  Button button_2 (.out(button_2_out));
  DipSwitch #(.number(2)) dipswitch_1 (.sw1(dipswitch_1_sw1), .sw2(dipswitch_1_sw2));
  or or_1 (or_1_out, button_1_out, dipswitch_1_sw1);
  ClearRAM clearram_1 (
    .ResetIn(or_1_out), .ResetOut(clearram_1_resetout), .DataOut(clearram_1_dataout),
    .AddrOut(clearram_1_addrout), .ClockOut(clearram_1_clockout));
  or or_2 (or_2_out, clearram_1_resetout, button_2_out, dipswitch_1_sw2);
  Accumulator accumulator_1 (
    .DataOut(accumulator_1_dataout), .DataIn(clearram_1_dataout), .Set(controlunit_1_acc_set),
    .Reset(or_2_out));
  Output output_1 (
    .DataOut(clearram_1_dataout), .DataIn(arithmaticlogicunit_1_output), .Set(controlunit_1_out_set),
    .Reset(or_2_out), .Enable(controlunit_1_out_enable));
  ArithmaticLogicUnit arithmaticlogicunit_1 (
    .Output(arithmaticlogicunit_1_output), .FlagsOut(arithmaticlogicunit_1_flagsout),
    .InputA(clearram_1_dataout), .InputB(accumulator_1_dataout), .Operation(controlunit_1_aluoperation),
    .FlagsIn(flags_1_flagsoutalu));
  Flags flags_1 (
    .FlagsOutALU(flags_1_flagsoutalu), .FlagsOutCU(flags_1_flagsoutcu),
    .FlagsIn(arithmaticlogicunit_1_flagsout), .Set(controlunit_1_flags_set), .Reset(or_2_out));
  InstructionReg instructionreg_1 (
    .InstructionOut(instructionreg_1_instructionout), .InstructionIn(clearram_1_dataout),
    .Set(controlunit_1_ir_set), .Reset(or_2_out));
  TempAddress tempaddress_1 (
    .AddressOut(tempaddress_1_addressout), .Data_In(clearram_1_dataout), .SetLow(controlunit_1_temp_lowset),
    .SetHigh(controlunit_1_temp_highset), .Reset(or_2_out));
  ControlUnit controlunit_1 (
    .RAM_Enable(controlunit_1_ram_enable), .RAM_Set(controlunit_1_ram_set),
    .RAM_Store(controlunit_1_ram_store), .GPR_Set(controlunit_1_gpr_set),
    .GPR_Enable(controlunit_1_gpr_enable), .GPR_Store(controlunit_1_gpr_store),
    .PC_Set(controlunit_1_pc_set), .PC_Load(controlunit_1_pc_load), .OUT_Set(controlunit_1_out_set),
    .Flags_Set(controlunit_1_flags_set), .TempSelect(controlunit_1_tempselect),
    .ACC_Set(controlunit_1_acc_set), .OUT_Enable(controlunit_1_out_enable),
    .Temp_LowSet(controlunit_1_temp_lowset), .Temp_HighSet(controlunit_1_temp_highset),
    .SP_Out(controlunit_1_sp_out), .IncSP(controlunit_1_incsp), .DecSP(controlunit_1_decsp),
    .RegSelect(controlunit_1_regselect), .IR_Set(controlunit_1_ir_set),
    .ALUOperation(controlunit_1_aluoperation), .Instruction(instructionreg_1_instructionout),
    .Reset(or_2_out), .Flags(flags_1_flagsoutcu));
  ProgramCounter programcounter_1 (
    .AddressOut(programcounter_1_addressout), .AddressIn(tempaddress_1_addressout),
    .Load(controlunit_1_pc_load), .Set(controlunit_1_pc_set), .Reset(or_2_out));
  Multiplexer #(.enable("false"), .width(16)) multiplexer_1 (
    .in0(programcounter_1_addressout), .in1(tempaddress_1_addressout), .out(multiplexer_1_out),
    .sel(controlunit_1_tempselect));
  Multiplexer #(.enable("false"), .width(16)) multiplexer_2 (
    .in0(multiplexer_1_out), .in1({8'h1, gpr_block_1_stack_pointer_out}), .out(multiplexer_2_out),
    .sel(controlunit_1_sp_out));
  RAMGate ramgate_1 (
    .AddrOut(ramgate_1_addrout), .LoadOut(ramgate_1_loadout), .StoreOut(ramgate_1_storeout),
    .ClockOut(ramgate_1_clockout), .AddrIn(multiplexer_2_out), .ClearAddr(clearram_1_addrout),
    .LoadIn(controlunit_1_ram_enable), .StoreIn(controlunit_1_ram_store), .ClockIn(controlunit_1_ram_set),
    .ClearClock(clearram_1_clockout), .ClearEnable(clearram_1_resetout));
  RAM #(.addrWidth(16), .databus("bidir")) Main_RAM (
    .addr(ramgate_1_addrout), .data(clearram_1_dataout));  // open: we, oe, clk
  GPR_Block gpr_block_1 (
    .Data_Out(clearram_1_dataout), .Stack_Pointer_Out(gpr_block_1_stack_pointer_out),
    .IncSP(controlunit_1_incsp), .DecSP(controlunit_1_decsp), .Write_Enable(controlunit_1_gpr_store),
    .Data_In(clearram_1_dataout), .Register_Select(controlunit_1_regselect), .Clock(controlunit_1_gpr_set),
    .Clear(or_2_out), .Read_Enable(controlunit_1_gpr_enable));

  // Notes on the sheet:
  //   Clear RAM
  //   Reset CPU
endmodule

// Control Unit
module ControlUnit (
  input  Reset,
  input  [1:0] Flags,
  input  [7:0] Instruction,
  output IR_Set,
  output RAM_Enable,
  output RAM_Set,
  output RAM_Store,
  output GPR_Set,
  output GPR_Enable,
  output GPR_Store,
  output PC_Set,
  output PC_Load,
  output TempSelect,
  output ACC_Set,
  output OUT_Enable,
  output Temp_LowSet,
  output Temp_HighSet,
  output SP_Out,
  output IncSP,
  output DecSP,
  output OUT_Set,
  output Flags_Set,
  output [2:0] RegSelect,
  output [3:0] ALUOperation
);

  wire and_1_out, and_2_out, and_3_out, and_4_out, and_5_out, and_6_out, and_7_out, and_8_out, and_9_out,
       and_10_out, and_11_out, and_12_out, and_13_out, and_14_out, and_15_out, and_16_out, and_17_out,
       and_18_out, and_19_out, and_20_out, and_21_out, and_22_out, and_23_out, buffer_1_out, buffer_2_out,
       buffer_3_out, buffer_4_out, buffer_5_out, buffer_6_out, buffer_7_out, buffer_8_out, buffer_9_out,
       buffer_10_out, buffer_11_out, buffer_12_out, buffer_13_out, buffer_14_out, buffer_15_out,
       buffer_16_out, buffer_17_out, buffer_18_out, buffer_19_out, buffer_20_out, buffer_21_out,
       buffer_22_out, buffer_23_out, buffer_24_out, buffer_25_out, comparator_1_eq,
       conditionaljump_1_pc_load, conditionaljump_1_pc_set, conditionaljump_1_resetstepper, decoder_1_out0,
       decoder_1_out1, decoder_1_out2, decoder_1_out3, decoder_1_out4, decoder_1_out5, decoder_1_out6,
       decoder_1_out7, decoder_2_out0, decoder_2_out1, decoder_2_out2, decoder_2_out3, decoder_2_out4,
       decoder_2_out5, decoder_2_out6, decoder_2_out7, decoder_2_out8, decoder_2_out9, decoder_2_out10,
       decoder_2_out11, decoder_2_out12, decoder_2_out13, decoder_2_out14, load_temp_1_pc_set,
       load_temp_1_ram_enable, not_1_out, or_1_out, or_2_out, or_3_out, or_4_out, or_5_out, or_6_out,
       or_7_out, stepper_1_setep2low, stepper_1_step0low, stepper_1_step1high, stepper_1_step1low;

  or or_1 (or_1_out, or_7_out, Reset);
  Stepper stepper_1 (
    .Step0Low(stepper_1_step0low), .Step0High(IR_Set), .Step1Low(stepper_1_step1low),
    .Step1High(stepper_1_step1high), .Setep2Low(stepper_1_setep2low), .Reset(or_1_out));  // open: Step2High
  not not_1 (not_1_out, Instruction[7]);
  Decoder #(.select(3)) decoder_1 (
    .out0(decoder_1_out0), .out1(decoder_1_out1), .out2(decoder_1_out2), .out3(decoder_1_out3),
    .out4(decoder_1_out4), .out5(decoder_1_out5), .out6(decoder_1_out6), .out7(decoder_1_out7),
    .sel(Instruction[2:0]), .en(not_1_out));
  Comparator #(.mode("unsigned"), .width(4)) comparator_1 (
    .a(Instruction[6:3]), .b(4'b1111), .eq(comparator_1_eq));  // open: gt, lt
  Decoder #(.select(4)) decoder_2 (
    .out0(decoder_2_out0), .out1(decoder_2_out1), .out2(decoder_2_out2), .out3(decoder_2_out3),
    .out4(decoder_2_out4), .out5(decoder_2_out5), .out6(decoder_2_out6), .out7(decoder_2_out7),
    .out8(decoder_2_out8), .out9(decoder_2_out9), .out10(decoder_2_out10), .out11(decoder_2_out11),
    .out12(decoder_2_out12), .out13(decoder_2_out13), .out14(decoder_2_out14), .sel(Instruction[6:3]),
    .en(not_1_out));  // open: out15
  or or_2 (or_2_out, decoder_1_out0, decoder_1_out5, decoder_1_out6);
  or or_3 (or_3_out, decoder_2_out7, decoder_2_out8, decoder_2_out9, decoder_2_out10, decoder_2_out11, decoder_2_out12, decoder_2_out13, decoder_2_out14);
  and and_1 (and_1_out, IR_Set, decoder_1_out1, decoder_2_out0);
  and and_2 (and_2_out, stepper_1_step1low, decoder_1_out1, decoder_2_out0);
  or or_4 (or_4_out, decoder_1_out2, decoder_1_out3, decoder_1_out7);
  and and_3 (and_3_out, stepper_1_step1high, decoder_1_out2, decoder_2_out0);
  and and_4 (and_4_out, stepper_1_setep2low, decoder_1_out2, decoder_2_out0);
  and and_5 (and_5_out, stepper_1_step1high, decoder_1_out3, decoder_2_out0);
  and and_6 (and_6_out, stepper_1_setep2low, decoder_1_out3, decoder_2_out0);
  and and_7 (and_7_out, IR_Set, decoder_1_out4, decoder_2_out0);
  and and_8 (and_8_out, stepper_1_step1low, decoder_1_out4, decoder_2_out0);
  and and_9 (and_9_out, stepper_1_setep2low, decoder_1_out7, decoder_2_out0);
  and and_10 (and_10_out, IR_Set, decoder_2_out1);
  and and_11 (and_11_out, stepper_1_step1low, decoder_2_out1);
  and and_12 (and_12_out, stepper_1_step1high, decoder_2_out2);
  and and_13 (and_13_out, stepper_1_setep2low, decoder_2_out2);
  and and_14 (and_14_out, IR_Set, decoder_2_out3);
  and and_15 (and_15_out, stepper_1_step1low, decoder_2_out3);
  and and_16 (and_16_out, IR_Set, decoder_2_out4);
  and and_17 (and_17_out, stepper_1_step1low, decoder_2_out4);
  and and_18 (and_18_out, stepper_1_step1high, decoder_2_out5);
  and and_19 (and_19_out, stepper_1_setep2low, decoder_2_out5);
  and and_20 (and_20_out, stepper_1_step1low, decoder_2_out0, or_2_out);
  and and_21 (and_21_out, stepper_1_step1low, or_3_out);
  and and_22 (and_22_out, decoder_2_out0, or_4_out);
  buf buffer_1 (buffer_1_out, and_9_out);
  buf buffer_2 (buffer_2_out, buffer_1_out);
  buf buffer_3 (buffer_3_out, buffer_2_out);
  buf buffer_4 (buffer_4_out, and_10_out);
  buf buffer_5 (buffer_5_out, buffer_4_out);
  buf buffer_6 (buffer_6_out, buffer_5_out);
  buf buffer_7 (buffer_7_out, and_12_out);
  buf buffer_8 (buffer_8_out, buffer_7_out);
  buf buffer_9 (buffer_9_out, buffer_8_out);
  buf buffer_10 (buffer_10_out, and_14_out);
  buf buffer_11 (buffer_11_out, buffer_10_out);
  buf buffer_12 (buffer_12_out, buffer_11_out);
  buf buffer_13 (buffer_13_out, and_18_out);
  buf buffer_14 (buffer_14_out, buffer_13_out);
  buf buffer_15 (buffer_15_out, buffer_14_out);
  ConditionalJump conditionaljump_1 (
    .PC_Load(conditionaljump_1_pc_load), .PC_Set(conditionaljump_1_pc_set),
    .ResetStepper(conditionaljump_1_resetstepper), .Flags(Flags), .Step1High(stepper_1_step1high),
    .Step2Low(stepper_1_setep2low), .Condition(Instruction[2:0]), .Enable(decoder_2_out6),
    .Step1Low(stepper_1_step1low));
  and and_23 (and_23_out, IR_Set, Instruction[7]);
  and and_24 (OUT_Set, stepper_1_step1low, Instruction[7], ~comparator_1_eq);  // AND_Gate
  and and_25 (Flags_Set, stepper_1_step1low, Instruction[7]);
  or or_5 (or_5_out, and_20_out, and_21_out);
  or or_6 (or_6_out, and_22_out, decoder_2_out2, decoder_2_out5, decoder_2_out6);
  buf buffer_16 (buffer_16_out, buffer_3_out);
  buf buffer_17 (buffer_17_out, buffer_16_out);
  buf buffer_18 (buffer_18_out, buffer_6_out);
  buf buffer_19 (buffer_19_out, buffer_18_out);
  buf buffer_20 (buffer_20_out, buffer_9_out);
  buf buffer_21 (buffer_21_out, buffer_20_out);
  buf buffer_22 (buffer_22_out, buffer_12_out);
  buf buffer_23 (buffer_23_out, buffer_22_out);
  buf buffer_24 (buffer_24_out, buffer_15_out);
  buf buffer_25 (buffer_25_out, buffer_24_out);
  Load_Temp load_temp_1 (
    .RAM_Enable(load_temp_1_ram_enable), .PC_Set(load_temp_1_pc_set), .Temp_SetLow(Temp_LowSet),
    .Temp_SetHigh(Temp_HighSet), .Step0High(IR_Set), .Step1Low(stepper_1_step1low),
    .Step1High(stepper_1_step1high), .Enable(or_6_out));
  or or_7 (or_7_out, or_5_out, and_2_out, and_4_out, and_8_out, and_6_out, buffer_17_out, Flags_Set, and_11_out, and_13_out, and_15_out, and_17_out, and_19_out, conditionaljump_1_resetstepper);
  or or_8 (RAM_Enable, stepper_1_step0low, and_1_out, load_temp_1_ram_enable, and_5_out, buffer_19_out, buffer_21_out);
  or or_9 (RAM_Set, and_4_out, and_19_out);
  or or_10 (RAM_Store, and_3_out, buffer_25_out);
  or or_11 (GPR_Set, and_11_out, and_13_out, and_15_out);
  or or_12 (GPR_Enable, and_16_out, and_23_out, buffer_25_out);
  or or_13 (GPR_Store, buffer_19_out, buffer_21_out, buffer_23_out);
  or or_14 (PC_Set, IR_Set, and_2_out, load_temp_1_pc_set, buffer_17_out, and_11_out, and_13_out, conditionaljump_1_pc_set);
  or or_15 (PC_Load, and_9_out, conditionaljump_1_pc_load);
  or or_16 (TempSelect, and_3_out, and_5_out, buffer_21_out, buffer_25_out);
  or or_17 (ACC_Set, and_2_out, and_6_out, and_8_out, and_17_out);
  or or_18 (OUT_Enable, and_3_out, and_7_out, buffer_23_out);
  or or_19 (SP_Out, 1'b0, 1'b0, 1'b0, 1'b0, 1'b0, 1'b0);
  or or_20 (IncSP, 1'b0, 1'b0, 1'b0, 1'b0, 1'b0, 1'b0);
  or or_21 (DecSP, 1'b0, 1'b0, 1'b0, 1'b0, 1'b0, 1'b0);

  assign ALUOperation = Instruction[6:3];
  assign RegSelect = Instruction[2:0];
endmodule

// Arithmatic Logic Unit
module ArithmaticLogicUnit (
  input  [7:0] InputA,
  input  [7:0] InputB,
  input  [1:0] FlagsIn,
  input  [3:0] Operation,
  output [7:0] Output,
  output [1:0] FlagsOut
);

  wire adder_1_cout, adder_2_cout, and_2_out, comparator_1_eq, comparator_2_eq, subtractor_1_bout,
       subtractor_2_bout;
  wire [2:0] bit_extender_1_out;
  wire [7:0] adder_1_out, adder_2_out, and_1_out, multiplier_1_cout, multiplier_1_out, nand_1_out,
       negator_1_out, nor_1_out, not_1_out, or_1_out, shifter_1_out, shifter_2_out, subtractor_1_out,
       subtractor_2_out, xor_1_out;

  Adder adder_1 (.a(InputA), .b(InputB), .out(adder_1_out), .cin(and_2_out), .cout(adder_1_cout));
  Subtractor subtractor_1 (.a(InputA), .b(InputB), .out(subtractor_1_out), .bout(subtractor_1_bout));  // open: bin
  Negator negator_1 (.in(InputA), .out(negator_1_out));
  Adder adder_2 (.a(InputA), .b(8'h1), .out(adder_2_out), .cout(adder_2_cout));  // open: cin
  Subtractor subtractor_2 (.a(InputA), .b(8'h1), .out(subtractor_2_out), .bout(subtractor_2_bout));  // open: bin
  Multiplier multiplier_1 (.a(InputA), .b(InputB), .out(multiplier_1_out), .cout(multiplier_1_cout));  // open: cin
  Comparator #(.mode("unsigned")) comparator_1 (
    .a(multiplier_1_cout), .b({8{1'b0}}), .eq(comparator_1_eq));  // open: gt, lt
  assign and_1_out = InputA & InputB;  // AND_Gate and_1, 8 bits wide
  assign nand_1_out = ~(InputA & InputB);  // NAND_Gate nand_1, 8 bits wide
  assign or_1_out = InputA | InputB;  // OR_Gate or_1, 8 bits wide
  assign nor_1_out = ~(InputA | InputB);  // NOR_Gate nor_1, 8 bits wide
  assign not_1_out = ~InputA;  // NOT_Gate not_1, 8 bits wide
  assign xor_1_out = InputA ^ InputB;  // XOR_Gate xor_1, 8 bits wide
  Bit_Extender #(.out_width(3)) bit_extender_1 (.in(InputB), .out(bit_extender_1_out));
  Shifter #(.shift("lr")) shifter_1 (.in(InputA), .\dist (bit_extender_1_out), .out(shifter_1_out));
  Shifter shifter_2 (.in(InputA), .\dist (bit_extender_1_out), .out(shifter_2_out));
  Multiplexer #(.enable("false"), .select(4), .width(8)) multiplexer_1 (
    .in0(adder_1_out), .in1(adder_1_out), .in2(subtractor_1_out), .in3(negator_1_out), .in4(adder_2_out),
    .in5(subtractor_2_out), .in6(multiplier_1_out), .in7(and_1_out), .in8(nand_1_out), .in9(or_1_out),
    .in10(nor_1_out), .in11(not_1_out), .in12(xor_1_out), .in13(shifter_1_out), .in14(shifter_2_out),
    .in15(subtractor_1_out), .out(Output), .sel(Operation));
  Multiplexer #(.enable("false"), .select(4)) multiplexer_2 (
    .in0(adder_1_cout), .in1(adder_1_cout), .in2(subtractor_1_bout), .in3(1'b0), .in4(adder_2_cout),
    .in5(subtractor_2_bout), .in6(comparator_1_eq), .in7(1'b0), .in8(1'b0), .in9(1'b0), .in10(1'b0),
    .in11(1'b0), .in12(1'b0), .in13(1'b0), .in14(1'b0), .in15(subtractor_1_bout), .out(FlagsOut[1]),
    .sel(Operation));
  and and_2 (and_2_out, FlagsIn[1], comparator_2_eq);
  Comparator #(.mode("unsigned"), .width(4)) comparator_2 (
    .a(Operation), .b(4'b0000), .eq(comparator_2_eq));  // open: gt, lt
  Comparator #(.mode("unsigned")) comparator_3 (.a(Output), .b({8{1'b0}}), .eq(FlagsOut[0]));  // open: gt, lt
endmodule

// Temp
module TempAddress (
  input  [7:0] Data_In,
  input  SetLow,
  input  SetHigh,
  input  Reset,
  output [15:0] AddressOut
);

  Register TempLow (.D(Data_In), .clk(SetLow), .Q(AddressOut[7:0]), .clr(Reset));  // open: en
  Register TempHigh (.D(Data_In), .clk(SetHigh), .Q(AddressOut[15:8]), .clr(Reset));  // open: en
endmodule

module Accumulator (
  input  [7:0] DataIn,
  input  Set,
  input  Reset,
  output [7:0] DataOut
);

  Register Accumulator (.D(DataIn), .clk(Set), .Q(DataOut), .clr(Reset));  // open: en
endmodule

module Output (
  input  [7:0] DataIn,
  input  Set,
  input  Reset,
  input  Enable,
  output [7:0] DataOut
);

  wire [7:0] Output_q;

  Register Output (.D(DataIn), .clk(Set), .Q(Output_q), .clr(Reset));  // open: en
  assign DataOut = Enable ? Output_q : 8'bz;  // Controlled_Buffer controlled_buffer_1
endmodule

module Flags (
  input  [1:0] FlagsIn,
  input  Set,
  input  Reset,
  output [1:0] FlagsOutALU,
  output [1:0] FlagsOutCU
);

  Register #(.width(2)) Flags (.D(FlagsIn), .clk(Set), .Q(FlagsOutALU), .clr(Reset));  // open: en

  assign FlagsOutCU = FlagsOutALU;
endmodule

// PC
module ProgramCounter (
  input  [15:0] AddressIn,
  input  Load,
  input  Set,
  input  Reset,
  output [15:0] AddressOut
);

  wire [15:0] adder_1_out, multiplexer_1_out;

  Register #(.width(16)) ProgramCounter (.D(multiplexer_1_out), .clk(Set), .Q(AddressOut), .clr(Reset));  // open: en
  Adder #(.width(16)) adder_1 (.a(AddressOut), .b({16{1'b0}}), .out(adder_1_out), .cin(1'b1));  // open: cout
  Multiplexer #(.enable("false"), .width(16)) multiplexer_1 (
    .in0(adder_1_out), .in1(AddressIn), .out(multiplexer_1_out), .sel(Load));
endmodule

// Instruction
module InstructionReg (
  input  [7:0] InstructionIn,
  input  Set,
  input  Reset,
  output [7:0] InstructionOut
);

  Register Instruction (.D(InstructionIn), .clk(Set), .Q(InstructionOut), .clr(Reset));  // open: en
endmodule

module Stepper (
  input  Reset,
  output Step0Low,
  output Step0High,
  output Step1Low,
  output Step1High,
  output Setep2Low,
  output Step2High
);

  wire clock_1_out, not_1_out, or_1_out, or_2_out, or_3_out, or_4_out, or_5_out, s_r_ff_1_q, s_r_ff_2_q,
       s_r_ff_3_q, s_r_ff_4_q, s_r_ff_5_q, s_r_ff_6_q;

  Clock clock_1 (.out(clock_1_out));
  S_R_Flip_Flop #(.trigger("falling")) s_r_ff_1 (
    .S(s_r_ff_6_q), .R(1'b0), .clk(clock_1_out), .Q(s_r_ff_1_q), .reset(s_r_ff_2_q), .preset(Reset));  // open: Qn
  not not_1 (not_1_out, Reset);
  and and_1 (Step0Low, s_r_ff_1_q, not_1_out, ~s_r_ff_2_q);  // AND_Gate
  S_R_Flip_Flop s_r_ff_2 (
    .S(s_r_ff_1_q), .R(1'b0), .clk(clock_1_out), .Q(s_r_ff_2_q), .reset(or_1_out));  // open: Qn, preset
  or or_1 (or_1_out, Reset, s_r_ff_3_q);
  S_R_Flip_Flop #(.trigger("falling")) s_r_ff_3 (
    .S(s_r_ff_2_q), .R(1'b0), .clk(clock_1_out), .Q(s_r_ff_3_q), .reset(or_2_out));  // open: Qn, preset
  or or_2 (or_2_out, Reset, s_r_ff_4_q);
  and and_2 (Step0High, s_r_ff_2_q, not_1_out, ~s_r_ff_3_q);  // AND_Gate
  S_R_Flip_Flop s_r_ff_4 (
    .S(s_r_ff_3_q), .R(1'b0), .clk(clock_1_out), .Q(s_r_ff_4_q), .reset(or_3_out));  // open: Qn, preset
  or or_3 (or_3_out, Reset, s_r_ff_5_q);
  and and_3 (Step1Low, s_r_ff_3_q, not_1_out, ~s_r_ff_4_q);  // AND_Gate
  S_R_Flip_Flop #(.trigger("falling")) s_r_ff_5 (
    .S(s_r_ff_4_q), .R(1'b0), .clk(clock_1_out), .Q(s_r_ff_5_q), .reset(or_4_out));  // open: Qn, preset
  or or_4 (or_4_out, Reset, s_r_ff_6_q);
  and and_4 (Step1High, s_r_ff_4_q, not_1_out, ~s_r_ff_5_q);  // AND_Gate
  S_R_Flip_Flop s_r_ff_6 (
    .S(s_r_ff_5_q), .R(1'b0), .clk(clock_1_out), .Q(s_r_ff_6_q), .reset(or_5_out));  // open: Qn, preset
  or or_5 (or_5_out, Reset, s_r_ff_1_q);
  and and_5 (Setep2Low, s_r_ff_5_q, not_1_out, ~s_r_ff_6_q);  // AND_Gate
  and and_6 (Step2High, s_r_ff_6_q, not_1_out, ~s_r_ff_1_q);  // AND_Gate
endmodule

// Load Address
module Load_Temp (
  input  Step0High,
  input  Step1Low,
  input  Step1High,
  input  Enable,
  output RAM_Enable,
  output PC_Set,
  output Temp_SetLow,
  output Temp_SetHigh
);

  wire buffer_1_out, or_1_out, or_2_out;

  buf buffer_1 (buffer_1_out, Step1High);
  or or_1 (or_1_out, Step0High, Step1Low);
  and and_1 (RAM_Enable, or_1_out, Enable);
  or or_2 (or_2_out, Step1Low, buffer_1_out);
  and and_2 (PC_Set, or_2_out, Enable);
  and and_3 (Temp_SetLow, Step1Low, Enable);
  and and_4 (Temp_SetHigh, Step1High, Enable);
endmodule

// Conditional Jump
module ConditionalJump (
  input  [1:0] Flags,
  input  Step1High,
  input  Step2Low,
  input  Step1Low,
  input  [2:0] Condition,
  input  Enable,
  output PC_Load,
  output PC_Set,
  output ResetStepper
);

  wire and_1_out, and_2_out, and_3_out, and_4_out, and_5_out, and_6_out, and_7_out, and_8_out, and_9_out,
       and_10_out, buffer_1_out, buffer_2_out, buffer_3_out, buffer_4_out, buffer_5_out, buffer_6_out,
       buffer_7_out, buffer_8_out, buffer_9_out, buffer_10_out, buffer_11_out, buffer_12_out, buffer_13_out,
       d_ff_1_q, decoder_1_out0, decoder_1_out1, decoder_1_out2, decoder_1_out3, decoder_1_out4,
       decoder_1_out5, not_1_out, not_2_out, or_1_out;

  not not_1 (not_1_out, Flags[1]);
  not not_2 (not_2_out, Flags[0]);
  Decoder #(.select(3)) decoder_1 (
    .out0(decoder_1_out0), .out1(decoder_1_out1), .out2(decoder_1_out2), .out3(decoder_1_out3),
    .out4(decoder_1_out4), .out5(decoder_1_out5), .sel(Condition), .en(Enable));  // open: out6, out7
  and and_1 (and_1_out, not_2_out, decoder_1_out0);
  and and_2 (and_2_out, Flags[0], decoder_1_out1);
  and and_3 (and_3_out, Flags[1], decoder_1_out2);
  and and_4 (and_4_out, not_1_out, decoder_1_out3);
  and and_5 (and_5_out, not_2_out, not_1_out, decoder_1_out4);
  and and_6 (and_6_out, Flags[0], not_1_out, decoder_1_out5);
  and and_7 (and_7_out, not_2_out, Flags[1], decoder_1_out5);
  and and_8 (and_8_out, Flags[0], Flags[1], decoder_1_out5);
  or or_1 (or_1_out, and_1_out, and_2_out, and_3_out, and_4_out, and_5_out, and_6_out, and_7_out, and_8_out);
  D_Flip_Flop d_ff_1 (.D(or_1_out), .clk(Step1Low), .Q(d_ff_1_q), .reset(buffer_1_out));  // open: Qn, preset
  and and_9 (and_9_out, Step1High, Enable, d_ff_1_q);
  and and_10 (and_10_out, Step2Low, Enable, d_ff_1_q);
  and and_11 (ResetStepper, Step2Low, Enable);
  buf buffer_1 (buffer_1_out, buffer_2_out);
  buf buffer_2 (buffer_2_out, buffer_3_out);
  buf buffer_3 (buffer_3_out, buffer_12_out);
  buf buffer_4 (buffer_4_out, and_9_out);
  buf buffer_5 (buffer_5_out, buffer_4_out);
  buf buffer_6 (buffer_6_out, buffer_5_out);
  buf buffer_7 (buffer_7_out, buffer_6_out);
  buf buffer_8 (buffer_8_out, and_10_out);
  buf buffer_9 (buffer_9_out, buffer_8_out);
  buf buffer_10 (buffer_10_out, buffer_9_out);
  buf buffer_11 (buffer_11_out, buffer_10_out);
  buf buffer_12 (buffer_12_out, buffer_13_out);
  buf buffer_13 (buffer_13_out, ResetStepper);
  buf buffer_14 (PC_Load, buffer_7_out);
  buf buffer_15 (PC_Set, buffer_11_out);
endmodule

module ClearGPR (
  input  ResetIn,
  output ResetOut,
  output [7:0] DataOut,
  output [2:0] AddrOut,
  output ClockOut
);

  wire counter_1_carry;
  wire [3:3] counter_1_q;

  Counter #(.max('hf), .width(4)) counter_1 (
    .clr(counter_1_q[3]), .count(ResetOut), .clk(ClockOut), .carry(counter_1_carry),
    .Q({counter_1_q[3], AddrOut}));  // open: load, up, D
  Clock clock_1 (.out(ClockOut));
  S_R_Flip_Flop #(.trigger("high")) s_r_ff_1 (
    .clk(counter_1_carry), .Q(ResetOut), .reset(counter_1_q[3]), .preset(ResetIn));  // open: S, R, Qn
  assign DataOut = ResetOut ? {8{1'b0}} : 8'bz;  // Controlled_Buffer controlled_buffer_1
endmodule

module GPRGate (
  input  ClearEnable,
  input  [2:0] AddrIn,
  input  [2:0] ClearAddr,
  input  LoadIn,
  input  StoreIn,
  input  ClockIn,
  input  ClearClock,
  output [2:0] AddrOut,
  output LoadOut,
  output StoreOut,
  output ClockOut
);

  Multiplexer #(.enable("false"), .width(3)) multiplexer_1 (
    .in0(AddrIn), .in1(ClearAddr), .out(AddrOut), .sel(ClearEnable));
  and and_1 (LoadOut, ~ClearEnable, LoadIn);  // AND_Gate
  Multiplexer #(.enable("false")) multiplexer_2 (.in0(StoreIn), .in1(ClearEnable), .out(StoreOut), .sel(ClearEnable));
  Multiplexer #(.enable("false")) multiplexer_3 (.in0(ClockIn), .in1(ClearClock), .out(ClockOut), .sel(ClearEnable));
endmodule

module RAMGate (
  input  ClearEnable,
  input  [15:0] AddrIn,
  input  [15:0] ClearAddr,
  input  LoadIn,
  input  StoreIn,
  input  ClockIn,
  input  ClearClock,
  output [15:0] AddrOut,
  output LoadOut,
  output StoreOut,
  output ClockOut
);

  Multiplexer #(.enable("false"), .width(16)) multiplexer_1 (
    .in0(AddrIn), .in1(ClearAddr), .out(AddrOut), .sel(ClearEnable));
  and and_1 (LoadOut, ~ClearEnable, LoadIn);  // AND_Gate
  Multiplexer #(.enable("false")) multiplexer_2 (.in0(StoreIn), .in1(ClearEnable), .out(StoreOut), .sel(ClearEnable));
  Multiplexer #(.enable("false")) multiplexer_3 (.in0(ClockIn), .in1(ClearClock), .out(ClockOut), .sel(ClearEnable));
endmodule

module ClearRAM (
  input  ResetIn,
  output ResetOut,
  output [7:0] DataOut,
  output [15:0] AddrOut,
  output ClockOut
);

  wire counter_1_carry;
  wire [16:16] counter_1_q;

  Counter #(.max('h1ffff), .width(17)) counter_1 (
    .clr(counter_1_q[16]), .count(ResetOut), .clk(ClockOut), .carry(counter_1_carry),
    .Q({counter_1_q[16], AddrOut}));  // open: load, up, D
  Clock clock_1 (.out(ClockOut));
  S_R_Flip_Flop #(.trigger("high")) s_r_ff_1 (
    .clk(counter_1_carry), .Q(ResetOut), .reset(counter_1_q[16]), .preset(ResetIn));  // open: S, R, Qn
  assign DataOut = ResetOut ? {8{1'b0}} : 8'bz;  // Controlled_Buffer controlled_buffer_1
endmodule

module GPR_Block (
  input  [7:0] Data_In,
  input  Write_Enable,
  input  [2:0] Register_Select,
  input  IncSP,
  input  DecSP,
  input  Clock,
  input  Clear,
  input  Read_Enable,
  output [7:0] Data_Out,
  output [7:0] Stack_Pointer_Out
);

  wire demultiplexer_1_out0, demultiplexer_1_out1, demultiplexer_1_out2, demultiplexer_1_out3,
       demultiplexer_1_out4, demultiplexer_1_out5, demultiplexer_1_out6, demultiplexer_1_out7, or_1_out;
  wire [7:0] adder_1_out, multiplexer_1_out, multiplexer_2_out, r0_q, r1_q, r2_q, r3_q, r4_q, r5_q, r6_q,
       subtractor_1_out;

  Adder adder_1 (.a(Stack_Pointer_Out), .b({8{1'b0}}), .out(adder_1_out), .cin(IncSP));  // open: cout
  Subtractor subtractor_1 (.a(Stack_Pointer_Out), .b({8{1'b0}}), .out(subtractor_1_out), .bin(DecSP));  // open: bout
  or or_1 (or_1_out, IncSP, DecSP);
  Multiplexer #(.enable("false"), .width(8)) multiplexer_1 (
    .in0(Data_In), .in1(multiplexer_2_out), .out(multiplexer_1_out), .sel(or_1_out));
  Multiplexer #(.enable("false"), .width(8)) multiplexer_2 (
    .in0(adder_1_out), .in1(subtractor_1_out), .out(multiplexer_2_out), .sel(DecSP));
  Demultiplexer #(.enable("false"), .select(3)) demultiplexer_1 (
    .out0(demultiplexer_1_out0), .out1(demultiplexer_1_out1), .out2(demultiplexer_1_out2),
    .out3(demultiplexer_1_out3), .out4(demultiplexer_1_out4), .out5(demultiplexer_1_out5),
    .out6(demultiplexer_1_out6), .out7(demultiplexer_1_out7), .in(Write_Enable), .sel(Register_Select));
  Register r0 (.D(Data_In), .en(demultiplexer_1_out0), .clk(Clock), .Q(r0_q), .clr(Clear));
  Register r1 (.D(Data_In), .en(demultiplexer_1_out1), .clk(Clock), .Q(r1_q), .clr(Clear));
  Register r2 (.D(Data_In), .en(demultiplexer_1_out2), .clk(Clock), .Q(r2_q), .clr(Clear));
  Register r3 (.D(Data_In), .en(demultiplexer_1_out3), .clk(Clock), .Q(r3_q), .clr(Clear));
  Register r4 (.D(Data_In), .en(demultiplexer_1_out4), .clk(Clock), .Q(r4_q), .clr(Clear));
  Register r5 (.D(Data_In), .en(demultiplexer_1_out5), .clk(Clock), .Q(r5_q), .clr(Clear));
  Register r6 (.D(Data_In), .en(demultiplexer_1_out6), .clk(Clock), .Q(r6_q), .clr(Clear));
  Register r7 (.D(multiplexer_1_out), .en(demultiplexer_1_out7), .clk(Clock), .Q(Stack_Pointer_Out), .clr(Clear));
  Multiplexer #(.disabled("Z"), .select(3), .width(8)) multiplexer_3 (
    .in0(r0_q), .in1(r1_q), .in2(r2_q), .in3(r3_q), .in4(r4_q), .in5(r5_q), .in6(r6_q),
    .in7(Stack_Pointer_Out), .out(Data_Out), .sel(Register_Select), .en(Read_Enable));

  // Other names for the same wires on the sheet: sp[7:0] = Stack_Pointer_Out; spIn[7:0] = Data_In
endmodule
