// Logisim project Demo CPU.circ as structural Verilog: 3 circuits, main circuit main
module main (
);

  wire button_1_out, button_2_out;

  Button button_1 (.out(button_1_out));
  Button button_2 (.out(button_2_out));
  CPU_Core cpu_core_1 (
    .Reset(button_1_out), .RAM_Clear(button_2_out));  // open: RAM_Set, RAM_Enable, Data_Out, Data_In, ADDR_Out, ADDR_In
endmodule

// CPU
module CPU_Core (
  input  [15:0] ADDR_In,
  input  [7:0] Data_In,
  input  Reset,
  input  RAM_Clear,
  output [15:0] ADDR_Out,
  output RAM_Set,
  output RAM_Enable,
  output [7:0] Data_Out
);

  wire arithmatic_logic_unit_1_clear_a, arithmatic_logic_unit_1_clear_b, arithmatic_logic_unit_1_clear_flags,
       arithmatic_logic_unit_1_set_flags, arithmatic_logic_unit_1_set_output, command_unit_1_acc_set,
       command_unit_1_alu_clock, command_unit_1_decrement_stack, command_unit_1_gpr_clear,
       command_unit_1_gpr_enable, command_unit_1_gpr_set, command_unit_1_iar_load_l,
       command_unit_1_iar_load_u, command_unit_1_iar_reset, command_unit_1_ier_clock,
       command_unit_1_ier_reset, command_unit_1_input_a_set, command_unit_1_load_from_iar,
       command_unit_1_load_from_stack, command_unit_1_mar_reset, command_unit_1_mar_set,
       command_unit_1_output_enable, command_unit_1_ram_set, command_unit_1_set_stack_address,
       command_unit_1_set_stack_data;
  wire [2:0] command_unit_1_gpr_select;
  wire [3:0] alu_flags_1_flags_out, arithmatic_logic_unit_1_flags, command_unit_1_alu_opcode;
  wire [7:0] accumulator_1_data_out, accumulator_2_data_out, arithmatic_logic_unit_1_output,
       instruction_execution_register_1_instruction_output, output_1_data_out;
  wire [15:0] instruction_address_register_1_to_mar, mar_stack_1_to_mar, memory_address_register_1_addr,
       memory_address_register_1_to_stack, multiplexer_1_out;

  Accumulator accumulator_1 (
    .Data_In(output_1_data_out), .Data_Out(accumulator_1_data_out), .Clear(arithmatic_logic_unit_1_clear_a),
    .Set(command_unit_1_input_a_set));
  Output output_1 (
    .Data_In(arithmatic_logic_unit_1_output), .Set(arithmatic_logic_unit_1_set_output),
    .Data_Out(output_1_data_out), .Clear(Reset), .Enable(command_unit_1_output_enable));  // open: Print_Out
  Accumulator accumulator_2 (
    .Data_In(output_1_data_out), .Data_Out(accumulator_2_data_out), .Clear(arithmatic_logic_unit_1_clear_b),
    .Set(command_unit_1_acc_set));
  Arithmatic_Logic_Unit arithmatic_logic_unit_1 (
    .Flags(arithmatic_logic_unit_1_flags), .Set_Flags(arithmatic_logic_unit_1_set_flags),
    .Clear_Flags(arithmatic_logic_unit_1_clear_flags), .Clock(command_unit_1_alu_clock),
    .Operation(command_unit_1_alu_opcode), .Input_A(accumulator_1_data_out),
    .Clear_B(arithmatic_logic_unit_1_clear_b), .Input_B(accumulator_2_data_out), .Reset(Reset),
    .Set_Output(arithmatic_logic_unit_1_set_output), .Output(arithmatic_logic_unit_1_output),
    .Clear_A(arithmatic_logic_unit_1_clear_a));
  ALU_Flags alu_flags_1 (
    .Flags_In(arithmatic_logic_unit_1_flags), .Set(arithmatic_logic_unit_1_set_flags),
    .Clear(arithmatic_logic_unit_1_clear_flags), .Flags_Out(alu_flags_1_flags_out));
  RAM #(.addrWidth(3)) ram_1 (
    .addr(command_unit_1_gpr_select), .data(output_1_data_out), .clk(command_unit_1_gpr_set),
    .ld(command_unit_1_gpr_enable), .clr(command_unit_1_gpr_clear));  // open: sel
  Instruction_Execution_Register instruction_execution_register_1 (
    .Instruction_Input(output_1_data_out),
    .Instruction_Output(instruction_execution_register_1_instruction_output),
    .Reset(command_unit_1_ier_reset), .Clock(command_unit_1_ier_clock));
  Command_Unit command_unit_1 (
    .Execute_Instruction(instruction_execution_register_1_instruction_output),
    .ALU_Opcode(command_unit_1_alu_opcode), .IER_Clock(command_unit_1_ier_clock),
    .IER_Reset(command_unit_1_ier_reset), .IAR_Load_L(command_unit_1_iar_load_l),
    .IAR_Reset(command_unit_1_iar_reset), .IAR_Load_U(command_unit_1_iar_load_u),
    .Output_Enable(command_unit_1_output_enable), .Reset(Reset), .ACC_Set(command_unit_1_acc_set),
    .ALU_Clock(command_unit_1_alu_clock), .ALU_Flags(alu_flags_1_flags_out),
    .Load_From_IAR(command_unit_1_load_from_iar), .Load_From_Stack(command_unit_1_load_from_stack),
    .MAR_Reset(command_unit_1_mar_reset), .MAR_Set(command_unit_1_mar_set), .RAM_Set(command_unit_1_ram_set),
    .RAM_Enable(RAM_Enable), .DEV_Set(RAM_Set), .GPR_Select(command_unit_1_gpr_select),
    .GPR_Set(command_unit_1_gpr_set), .GPR_Enable(command_unit_1_gpr_enable),
    .GPR_Clear(command_unit_1_gpr_clear), .Input_A_Set(command_unit_1_input_a_set),
    .Decrement_Stack(command_unit_1_decrement_stack), .Set_Stack_Address(command_unit_1_set_stack_address),
    .Set_Stack_Data(command_unit_1_set_stack_data));
  Instruction_Address_Register instruction_address_register_1 (
    .Address_In(output_1_data_out), .Set_Lower_Half(command_unit_1_iar_load_l),
    .Reset(command_unit_1_iar_reset), .Set_Upper_Half(command_unit_1_iar_load_u),
    .To_MAR(instruction_address_register_1_to_mar));
  MAR_Stack mar_stack_1 (
    .Decrement(command_unit_1_decrement_stack), .Set_Address(command_unit_1_set_stack_address),
    .Set(command_unit_1_set_stack_data), .Clear(Reset), .From_MAR(memory_address_register_1_to_stack),
    .To_MAR(mar_stack_1_to_mar));
  Memory_Address_Register memory_address_register_1 (
    .Set_Current(command_unit_1_mar_set), .Reset(command_unit_1_mar_reset),
    .Load_From_Return(command_unit_1_load_from_stack), .Load_From_IAR(command_unit_1_load_from_iar),
    .ADDR(memory_address_register_1_addr), .From_IAR(instruction_address_register_1_to_mar),
    .From_Stack(mar_stack_1_to_mar), .To_Stack(memory_address_register_1_to_stack));
  Multiplexer #(.width(16)) multiplexer_1 (
    .in0(memory_address_register_1_addr), .in1(instruction_address_register_1_to_mar),
    .out(multiplexer_1_out), .sel(1'b0), .en(1'b1));
  assign ADDR_Out = 1'b0 ? multiplexer_1_out : 16'bz;  // Controlled_Buffer controlled_buffer_1
  assign multiplexer_1_out = 1'b0 ? ADDR_In : 16'bz;  // Controlled_Buffer controlled_buffer_2
  RAM #(.addrWidth(16)) ram_2 (
    .addr(multiplexer_1_out), .data(output_1_data_out), .clk(RAM_Set), .ld(RAM_Enable), .clr(RAM_Clear));  // open: sel
  assign Data_Out = command_unit_1_ram_set ? output_1_data_out : 8'bz;  // Controlled_Buffer controlled_buffer_3
  assign output_1_data_out = 1'b0 ? Data_In : 8'bz;  // Controlled_Buffer controlled_buffer_4

  // Notes on the sheet:
  //   General Purpose Registers
  //   RAM
endmodule

// Stack
module MAR_Stack (
  input  Decrement,
  input  Clear,
  input  Set_Address,
  input  Set,
  input  [15:0] From_MAR,
  output [15:0] To_MAR
);

  wire [7:0] adder_1_out, multiplexer_1_out, register_1_q, subtractor_1_out;

  Adder adder_1 (.a(register_1_q), .b(8'h1), .out(adder_1_out));  // open: cin, cout
  Multiplexer #(.width(8), .disabled(0), .enable("false")) multiplexer_1 (
    .in0(adder_1_out), .in1(subtractor_1_out), .out(multiplexer_1_out), .sel(Decrement));
  Subtractor subtractor_1 (.a(register_1_q), .b(8'h1), .out(subtractor_1_out));  // open: bin, bout
  Register register_1 (.D(multiplexer_1_out), .Q(register_1_q), .clk(Set_Address), .clr(Clear));  // open: en
  RAM #(.dataWidth(16), .bus("separate")) ram_1 (
    .addr(register_1_q), .din(From_MAR), .data(To_MAR), .str(1'b1), .clk(Set), .ld(1'b1), .clr(Clear));  // open: sel
endmodule
