// Logisim project Demo8 No Roms.circ as structural Verilog
module Control_Unit (
  input  Clk,
  input  Clr,
  input  [7:0] Instruction,
  output IR_WE,
  output out_5,
  output out_6,
  output out_7,
  output out_8,
  output out_9,
  output PC_WH,
  output PC_WL,
  output [1:0] ADDR_SEL
);

  wire and_2_out, and_3_out, and_4_out, and_5_out, and_6_out, and_7_out, and_8_out, d_ff_1_q, d_ff_2_q,
       d_ff_3_q, d_ff_4_q, d_ff_5_q, d_ff_6_q, d_ff_7_q, d_ff_8_q, nand_1_out, nor_1_out, nor_2_out,
       not_1_out;
  wire [0:0] or_3_out;

  D_Flip_Flop d_ff_1 (.clk(Clk), .D(d_ff_8_q), .Q(d_ff_1_q), .preset(Clr));  // open: Qn, reset
  D_Flip_Flop d_ff_2 (.clk(Clk), .D(d_ff_1_q), .Q(d_ff_2_q), .reset(Clr));  // open: Qn, preset
  D_Flip_Flop d_ff_3 (.clk(Clk), .D(d_ff_2_q), .Q(d_ff_3_q), .reset(Clr));  // open: Qn, preset
  D_Flip_Flop d_ff_4 (.clk(Clk), .D(d_ff_3_q), .Q(d_ff_4_q), .reset(Clr));  // open: Qn, preset
  D_Flip_Flop d_ff_5 (.clk(Clk), .D(d_ff_4_q), .Q(d_ff_5_q), .reset(Clr));  // open: Qn, preset
  D_Flip_Flop d_ff_6 (.clk(Clk), .D(d_ff_5_q), .Q(d_ff_6_q), .reset(Clr));  // open: Qn, preset
  D_Flip_Flop d_ff_7 (.clk(Clk), .D(d_ff_6_q), .Q(d_ff_7_q), .reset(Clr));  // open: Qn, preset
  D_Flip_Flop d_ff_8 (.clk(Clk), .D(d_ff_7_q), .Q(d_ff_8_q), .reset(Clr));  // open: Qn, preset
  nor nor_1 (nor_1_out, Instruction[0], Instruction[2], Instruction[3]);
  nor nor_2 (nor_2_out, Instruction[5], Instruction[6], Instruction[7]);
  nand nand_1 (nand_1_out, nor_1_out, Instruction[1], Instruction[4], nor_2_out);
  and and_1 (IR_WE, d_ff_1_q, nand_1_out);
  and and_2 (and_2_out, d_ff_2_q, nand_1_out);
  and and_3 (and_3_out, d_ff_3_q, nand_1_out);
  and and_4 (and_4_out, d_ff_4_q, nand_1_out);
  and and_5 (and_5_out, d_ff_5_q, nand_1_out);
  and and_6 (and_6_out, d_ff_6_q, nand_1_out);
  and and_7 (and_7_out, d_ff_7_q, nand_1_out);
  and and_8 (and_8_out, d_ff_8_q, nand_1_out);
  not not_1 (not_1_out, nand_1_out);
  buf or_1 (PC_WH, IR_WE);  // OR_Gate
  buf or_2 (PC_WL, IR_WE);  // OR_Gate
  or or_3 (or_3_out[0], not_1_out, IR_WE);
  assign ADDR_SEL = {1'b0, or_3_out[0]};  // OR_Gate or_4, 2 bits wide OR_Gate

  // Notes on the sheet:
  //   Instruction Register
  //   Program Counter
endmodule
